# Fritzing sketch neklops_GH (saved by Fritzing 0.9.3b)
circuit board: 6.84096cm x 11.8239cm
breadboards: 1

parts:
  U1 = attiny85 [package=dip]
  CR2032 = Battery Holders [package=battcom_20mm_pth]
  MIDI/PGM1 = SWITCH-DPDT [package=eg2211]
  R1 = Rotary Potentiometer (Small) [maximum_resistance=10kΩ package=THT]
  R3 = Rotary Potentiometer (Small) [maximum_resistance=10kΩ package=THT]
  R4 = Resistor [tolerance=±5% resistance=47k package=THT]
  Pushbutton = SWITCH-MOMENTARY-2 [package=tactile-pth-12mm]
  S2 = SWITCH-MOMENTARY-2 [package=tactile-pth-12mm]
  R6 = Resistor [tolerance=±5% resistance=47k package=THT]
  TRS1 = Audio Jack (TRS) 3.5mm [package="4Ucon 08780 [THT]"]
  R2 = Rotary Potentiometer (Small) [maximum_resistance=10kΩ package=THT]
  LED1 = LED - 5mm [color="Red (633nm)" package="5 mm [THT]"]
  R5 = Resistor [tolerance=±5% resistance=47k package=THT]
  J3 = Generic female header - 1 pins [form="♀ (female)" package=THT]  # not connected
  J4 = Generic female header - 1 pins [form="♀ (female)" package=THT]  # not connected
  R7 = Resistor [tolerance=±5% resistance=2.2k package=THT]
  R8 = Resistor [tolerance=±5% resistance=4.7k package=THT]
  J5 = Generic female header - 1 pins [form="♀ (female)" package=THT]  # not connected
  J6 = Generic female header - 1 pins [form="♀ (female)" package=THT]  # not connected

nets:
  N1: U1.Pin_1, R4.Pin_0, Pushbutton.1, S2.2
  N2: U1.Pin_2, R1.wiper
  N3: U1.Pin_3, R2.wiper
  N4: U1.Pin_4, CR2032.-, R1.leg1, R3.leg1, TRS1.Sleeve, R2.leg1, LED1.cathode, R5.Pin_1, R8.Pin_1
  N5: U1.Pin_5, LED1.anode, R7.Pin_0
  N6: U1.Pin_6, R6.Pin_0
  N7: U1.Pin_7, R3.wiper
  N8: U1.Pin_8, MIDI/PGM1.5, R1.leg2, R3.leg2, R4.Pin_1, R2.leg2
  N9: CR2032.+, MIDI/PGM1.6
  N10: Pushbutton.2, R6.Pin_1
  N11: S2.1, R5.Pin_0
  N12: TRS1.Ring, TRS1.Tip, R7.Pin_1, R8.Pin_0

custom parts:
  Generic female header - 1 pins: Generic female header
  Generic female header - 1 pins: Generic female header
  Generic female header - 1 pins: Generic female header
  Generic female header - 1 pins: Generic female header
